# Fritzing sketch circuit (saved by Fritzing 0.9.10b)
breadboards: 1

parts:
  Part1 = Arduino Nano (Rev3.0)
  R1 = Basic Flex Resistor
  R2 = Basic Flex Resistor
  R3 = Basic Flex Resistor
  R4 = Basic Flex Resistor
  Grove1 = Grove 3 Axis Digital Accelerometer 16g
  R5 = Resistor [tolerance=±5% power=0.25 resistance=220 package=THT]
  R6 = Resistor [tolerance=±5% power=0.25 resistance=220 package=THT]
  R7 = Resistor [tolerance=±5% power=0.25 resistance=220 package=THT]
  R8 = Resistor [tolerance=±5% power=0.25 resistance=220 package=THT]
  Part2 = Adafruit MicroSD card breakout board [part_number="Adafruit #254"]
  SP1 = SPEAKER [package=pcb_mount_speaker]

nets:
  GND: Part1.GND, R1.pin_1, R2.pin_1, R3.pin_1, R4.pin_1, Grove1.GND, Part2.GND, SP1.+
  N1: Part1.D4, Part2.CS
  N2: Part1.D9, SP1.-
  N3: Part1.D11/MOSI, Part2.DI
  N4: Part1.D12/MISO, Part2.DO
  5V: Part1.5V, R5.Pin_1, R6.Pin_1, R7.Pin_1, R8.Pin_1, Part2.VCC
  N5: Part1.A5, Grove1.SCL
  N6: Part1.A4, Grove1.SDA
  N7: Part1.A3, R1.Pin_2, R8.Pin_0
  N8: Part1.A2, R2.Pin_2, R7.Pin_0
  N9: Part1.A1, R3.Pin_2, R6.Pin_0
  N10: Part1.A0, R4.Pin_2, R5.Pin_0
  3V3: Part1.3V3, Grove1.VCC
  N11: Part1.D13/SCK, Part2.CLK

custom parts:
  Adafruit MicroSD card breakout board: Not just a simple breakout board, this microSD adapter goes the extra mile - designed for ease of use. Onboard 5v->3v regulator provides 150mA for power-hungry cards 3v level shifting means you can use this with ease on either 3v or 5v systems Uses a proper level shifting chip, not resistors: less problems, and faster read/write access Use 3 or 4 digital pins to read and write 2Gb+ of storage!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
